# Fritzing sketch patchbay_breadboard-v1 (saved by Fritzing 0.9.3b)
breadboards: 1

parts:
  TRS1 = Audio Jack (TRS) 3.5mm [package="4Ucon 08780 [THT]"]
  TRS2 = Audio Jack (TRS) 3.5mm [package="4Ucon 08780 [THT]"]
  TRS3 = Audio Jack (TRS) 3.5mm [package="4Ucon 08780 [THT]"]
  TRS4 = Audio Jack (TRS) 3.5mm [package="4Ucon 08780 [THT]"]
  TRS10 = Audio Jack (TRS) 3.5mm [package="4Ucon 08780 [THT]"]
  TRS11 = Audio Jack (TRS) 3.5mm [package="4Ucon 08780 [THT]"]
  TRS12 = Audio Jack (TRS) 3.5mm [package="4Ucon 08780 [THT]"]
  S1 = Pushbutton [package="[THT]"]
  Part1 = Arduino Mega 2560 (Rev3)
  R1 = Resistor [tolerance=±5% resistance=1k package=THT]
  R3 = Resistor [tolerance=±5% resistance=1k package=THT]
  R4 = Resistor [tolerance=±5% resistance=1k package=THT]
  R5 = Resistor [tolerance=±5% resistance=1k package=THT]
  R6 = Resistor [tolerance=±5% resistance=1k package=THT]
  R7 = Resistor [tolerance=±5% resistance=1k package=THT]
  R8 = Resistor [tolerance=±5% resistance=1k package=THT]
  R9 = Resistor [tolerance=±5% resistance=1k package=THT]
  R10 = Resistor [tolerance=±5% resistance=1k package=THT]
  R11 = Resistor [tolerance=±5% resistance=1k package=THT]
  R12 = Resistor [tolerance=±5% resistance=1k package=THT]
  R13 = Resistor [tolerance=±5% resistance=1k package=THT]
  TRS13 = Audio Jack (TRS) 3.5mm [package="PG203J [THT]"]
  R14 = Resistor [tolerance=±5% resistance=1k package=THT]
  R15 = Resistor [tolerance=±5% resistance=1k package=THT]
  R16 = Resistor [tolerance=±5% resistance=1k package=THT]
  R17 = Resistor [tolerance=±5% resistance=1k package=THT]
  R18 = Resistor [tolerance=±5% resistance=1k package=THT]
  R19 = Resistor [tolerance=±5% resistance=1k package=THT]
  R20 = Resistor [tolerance=±5% resistance=1k package=THT]
  R21 = Resistor [tolerance=±5% resistance=1k package=THT]
  R22 = Resistor [tolerance=±5% resistance=1k package=THT]
  R23 = Resistor [tolerance=±5% resistance=1k package=THT]
  R24 = Resistor [tolerance=±5% resistance=1k package=THT]
  R25 = Resistor [tolerance=±5% resistance=1k package=THT]
  LED1 = RGB LED (com. cathode, rgb) [package="5 mm [THT]"]
  LED2 = RGB LED (com. cathode, rgb) [package="5 mm [THT]"]
  LED3 = RGB LED (com. cathode, rgb) [package="5 mm [THT]"]
  LED4 = RGB LED (com. cathode, rgb) [package="5 mm [THT]"]
  LED5 = RGB LED (com. cathode, rgb) [package="5 mm [THT]"]
  LED6 = RGB LED (com. cathode, rgb) [package="5 mm [THT]"]
  LED7 = RGB LED (com. cathode, rgb) [package="5 mm [THT]"]
  LED8 = RGB LED (com. cathode, rgb) [package="5 mm [THT]"]
  R26 = Resistor [tolerance=±5% resistance=1k package=THT]

nets:
  N1: TRS1.Sleeve, TRS1.Ring, TRS2.Sleeve, TRS2.Ring, TRS3.Sleeve, TRS3.Ring, TRS4.Sleeve, TRS4.Ring, TRS10.Sleeve, TRS10.Ring, TRS11.Sleeve, TRS11.Ring, TRS12.Sleeve, TRS12.Ring, R1.Pin_0, R3.Pin_0, R4.Pin_0, R5.Pin_0, R6.Pin_0, R7.Pin_0, R8.Pin_0, R9.Pin_0, R10.Pin_0, R11.Pin_0, R12.Pin_0, R13.Pin_0, TRS13.Sleeve, TRS13.Ring, R14.Pin_0, R15.Pin_0, R16.Pin_0, R17.Pin_0, R18.Pin_0, R19.Pin_0, R20.Pin_0, R21.Pin_0, R22.Pin_0, R23.Pin_0, R24.Pin_0, R25.Pin_0, LED1.common_cathode, LED2.common_cathode, LED3.common_cathode, LED4.common_cathode, LED5.common_cathode, LED6.common_cathode, LED7.common_cathode, LED8.common_cathode, R26.Pin_0
  N2: TRS1.Tip, Part1.A5
  N3: TRS2.Tip, Part1.A6
  N4: TRS3.Tip, Part1.A7
  N5: TRS4.Tip, Part1.A4
  N6: TRS10.Tip, Part1.A2
  N7: TRS11.Tip, Part1.A1
  N8: TRS12.Tip, Part1.A0
  N9: S1.Pin_1, S1.Pin_2, Part1.5V
  N10: S1.Pin_3, S1.Pin_4, Part1.D10_PWM, R26.Pin_1
  N11: Part1.A3, TRS13.Tip
  N12: Part1.D22, R1.Pin_1, LED1.red_anode
  N13: Part1.D23, R17.Pin_1, LED1.green_anode
  N14: Part1.D24, R3.Pin_1, LED1.blue_anode
  N15: Part1.D25, R5.Pin_1, LED2.red_anode
  N16: Part1.D26, R6.Pin_1, LED2.green_anode
  N17: Part1.D27, R7.Pin_1, LED2.blue_anode
  N18: Part1.D28, R8.Pin_1, LED3.red_anode
  N19: Part1.D29, R9.Pin_1, LED3.green_anode
  N20: Part1.D30, R10.Pin_1, LED3.blue_anode
  N21: Part1.D31, R11.Pin_1, LED4.red_anode
  N22: Part1.D32, R12.Pin_1, LED4.green_anode
  N23: Part1.D33, R13.Pin_1, LED4.blue_anode
  N24: Part1.D34, R14.Pin_1, LED5.red_anode
  N25: Part1.D35, R15.Pin_1, LED5.green_anode
  N26: Part1.D36, R4.Pin_1, LED5.blue_anode
  N27: Part1.D37, R16.Pin_1, LED6.red_anode
  N28: Part1.D38, R18.Pin_1, LED6.green_anode
  N29: Part1.D39, R19.Pin_1, LED6.blue_anode
  N30: Part1.D40, R20.Pin_1, LED7.red_anode
  N31: Part1.D41, R22.Pin_1, LED7.green_anode
  N32: Part1.D42, R21.Pin_1, LED7.blue_anode
  N33: Part1.D43, R23.Pin_1, LED8.red_anode
  N34: Part1.D44, R24.Pin_1, LED8.green_anode
  N35: Part1.D45, R25.Pin_1, LED8.blue_anode
